# Fritzing sketch board (saved by Fritzing 0.9.2b)
circuit board: 9.94291cm x 5.30975cm
breadboards: 1
stripboards: 1

parts:
  U1 = INA125 [package="DIP16 [THT]"]
  U2 = INA125 [package="DIP16 [THT]"]
  U3 = INA125 [package="DIP16 [THT]"]
  U4 = INA125 [package="DIP16 [THT]"]
  U5 = INA125 [package="DIP16 [THT]"]
  R1 = Resistor [tolerance=±5% resistance=20 package=THT]
  R2 = Resistor [tolerance=±5% resistance=20 package=THT]
  R3 = Resistor [tolerance=±5% resistance=20 package=THT]
  R4 = Resistor [tolerance=±5% resistance=20 package=THT]
  R5 = Resistor [tolerance=±5% resistance=75 package=THT]
  J1 = shrouded pin header, 20 pins [form="♂ (shrouded male)"]
  J2 = female pin header, 2 pins [form="♀ (female)"]
  J3 = female pin header, 2 pins [form="♀ (female)"]
  J4 = female pin header, 2 pins [form="♀ (female)"]
  J5 = female pin header, 2 pins [form="♀ (female)"]
  J6 = female pin header, 2 pins [form="♀ (female)"]
  J7 = female pin header, 9 pins [form="♀ (female)"]
  J8 = female pin header, 9 pins [form="♀ (female)"]
  Part1 = Arduino Mega 2560 (Rev3)
  10k_log = POT [package=pot_mammoth]
  U8 = AUDIO-JACK2 [package=audio-jack-3.5mm-smd]
  F1_2A = FUSE [part_number=2A package=fuse_5mm]
  IN_Right = female pin header, 1 pin [form="♀ (female)"]
  IN_Left = female pin header, 1 pin [form="♀ (female)"]
  GND = female pin header, 1 pin [form="♀ (female)"]
  VCC = female pin header, 1 pin [form="♀ (female)"]
  GND1 = female pin header, 1 pin [form="♀ (female)"]
  OUT_Right = female pin header, 1 pin [form="♀ (female)"]
  OUT_Left = female pin header, 1 pin [form="♀ (female)"]
  Audio_OUT_Left = Screw terminal - 2 pins [package=THT]
  Audio_OUT_Right = Screw terminal - 2 pins [package=THT]
  Power = screw terminal, 2 pins
  10k_log_2 = POT [package=pot_mammoth]

nets:
  N1: U1.V+, U1.SLEEP, U2.V+, U2.SLEEP, U3.V+, U3.SLEEP, U4.V+, U4.SLEEP, U5.V+, U5.SLEEP, J1.pin20, Part1.5V
  N2: U1.V-, U1.IAref, U1.VrefCON, U2.V-, U2.IAref, U2.VrefCON, U3.V-, U3.IAref, U3.VrefCON, U4.V-, U4.IAref, U4.VrefCON, U5.V-, U5.IAref, U5.VrefCON, J1.pin1, J1.pin7, J8.pin6, Part1.GND, GND.pin1, GND1.pin1, Audio_OUT_Left.pin1, Audio_OUT_Right.pin1, Power.pin2
  N3: U1.VrefOUT, U1.Vref5, U2.VrefOUT, U2.Vref5, U3.VrefOUT, U3.Vref5, U4.VrefOUT, U4.Vref5, U5.VrefOUT, U5.Vref5, Part1.AREF
  N4: U1.V+IN, J6.pin1
  N5: U1.V-IN, J6.pin2
  N6: U1.RG#7, R1.Pin_1
  N7: U1.RG#8, R1.Pin_0
  N8: U1.V0, U1.Sense, Part1.A0
  N9: U2.V+IN, J2.pin1
  N10: U2.V-IN, J2.pin2
  N11: U2.RG#7, R2.Pin_1
  N12: U2.RG#8, R2.Pin_0
  N13: U2.V0, U2.Sense, Part1.A1
  N14: U3.V+IN, J3.pin1
  N15: U3.V-IN, J3.pin2
  N16: U3.RG#7, R3.Pin_1
  N17: U3.RG#8, R3.Pin_0
  N18: U3.V0, U3.Sense, Part1.A2
  N19: U4.V+IN, J4.pin1
  N20: U4.V-IN, J4.pin2
  N21: U4.RG#7, R4.Pin_1
  N22: U4.RG#8, R4.Pin_0
  N23: U4.V0, U4.Sense, Part1.A3
  N24: U5.V+IN, J5.pin1
  N25: U5.V-IN, J5.pin2
  N26: U5.RG#7, R5.Pin_1
  N27: U5.RG#8, R5.Pin_0
  N28: U5.V0, U5.Sense, Part1.A4
  N29: J1.pin2, J8.pin1
  N30: J1.pin3, J8.pin2
  N31: J1.pin4, J8.pin3
  N32: J1.pin5, J8.pin4
  N33: J1.pin6, J8.pin5
  N34: J1.pin8, J8.pin7, F1_2A.2, Power.pin1
  N35: J1.pin9, J8.pin8, OUT_Right.pin1, Audio_OUT_Right.pin2
  N36: J1.pin10, J8.pin9, OUT_Left.pin1, Audio_OUT_Left.pin2
  N37: J1.pin11, J7.pin9
  N38: J1.pin12, J7.pin8
  N39: J1.pin13, J7.pin7
  N40: J1.pin14, J7.pin6
  N41: J1.pin15, J7.pin5
  N42: J1.pin16, J7.pin4
  N43: J1.pin17, J7.pin3
  N44: J1.pin18, J7.pin2
  N45: J1.pin19, J7.pin1
  N46: 10k_log.S, U8.SLEEVE, 10k_log_2.S
  N47: 10k_log.A, IN_Right.pin1
  N48: 10k_log.E, U8.TIP
  N49: U8.RING, 10k_log_2.E
  N50: F1_2A.1, VCC.pin1
  N51: IN_Left.pin1, 10k_log_2.A

custom parts:
  INA125: Instrumentation Amplifier
