# Fritzing sketch connector (saved by Fritzing 0.9.2b)
circuit board: 4.99904cm x 10.0025cm
breadboards: 1

parts:
  SensorB = female pin header, 4 pins [form="♀ (female)"]
  SensorC = female pin header, 4 pins [form="♀ (female)"]
  SensorD = female pin header, 4 pins [form="♀ (female)"]
  SensorE = female pin header, 4 pins [form="♀ (female)"]
  LED_Power = female pin header, 2 pins [form="♀ (female)"]
  AudioRechts = female pin header, 2 pins [form="♀ (female)"]
  J1 = shrouded pin header, 20 pins [form="♂ (shrouded male)"]
  SensorA = female pin header, 4 pins [form="♀ (female)"]
  AudioLinks = female pin header, 2 pins [form="♀ (female)"]

nets:
  N1: SensorB.pin1, J1.pin13
  N2: SensorB.pin2, SensorC.pin2, SensorD.pin2, SensorE.pin2, J1.pin11, SensorA.pin2
  N3: SensorB.pin3, SensorC.pin3, SensorD.pin3, SensorE.pin3, J1.pin10, SensorA.pin3
  N4: SensorB.pin4, J1.pin8
  N5: SensorC.pin1, J1.pin14
  N6: SensorC.pin4, J1.pin7
  N7: SensorD.pin1, J1.pin15
  N8: SensorD.pin4, J1.pin6
  N9: SensorE.pin1, J1.pin16
  N10: SensorE.pin4, J1.pin5
  N11: LED_Power.pin1, J1.pin18
  N12: LED_Power.pin2, AudioRechts.pin1, J1.pin17, AudioLinks.pin2
  N13: AudioRechts.pin2, J1.pin19
  N14: J1.pin9, SensorA.pin4
  N15: J1.pin12, SensorA.pin1
  N16: J1.pin20, AudioLinks.pin1
